# Fritzing sketch basic (saved by Fritzing 0.9.3b)
breadboards: 1

parts:
  Part1 = Arduino Uno (Rev3)
  R1 = Resistor [tolerance=±5% resistance=220 package="0805 [SMD]"]
  LED1 = LED - 3mm [color="Red (633nm)" package="3 mm [THT]"]
  R2 = Resistor [tolerance=±5% resistance=220 package="0805 [SMD]"]
  LED2 = LED - 3mm [color="Green (570nm)" package="3 mm [THT]"]

nets:
  N1: Part1.D8, R2.Pin_1
  N2: Part1.D9_PWM, R1.Pin_1
  N3: Part1.GND, LED1.cathode, LED2.cathode
  N4: R1.Pin_0, LED1.anode
  N5: R2.Pin_0, LED2.anode
