# Fritzing sketch basic_light (saved by Fritzing 0.9.3b)
breadboards: 1

parts:
  Part1 = Arduino Uno (Rev3)
  J1 = Piezo Speaker
  R1 = Photocell (LDR) [package=THT]
  R2 = Resistor [tolerance=±5% resistance=1.5k package=THT]

nets:
  N1: Part1.A0, R1.pin_0, R2.Pin_1
  N2: Part1.D8, J1.pin2
  N3: Part1.GND, J1.pin1, R2.Pin_0
  N4: Part1.5V, R1.pin_1
