# Fritzing sketch pass_or_repas (saved by Fritzing 0.9.2b)
breadboards: 1

parts:
  Componente1 = Arduino Uno (Rev3)
  S1 = Pushbutton [package="[THT]"]
  S2 = Pushbutton [package="[THT]"]
  S3 = Pushbutton [package="[THT]"]
  R1 = Resistor [tolerance=±5% resistance=10k package=THT]
  LED1 = LED - 5mm [color="Green (555nm)" package="5 mm [THT]"]
  R2 = Resistor [tolerance=±5% resistance=220 package=THT]
  R3 = Resistor [tolerance=±5% resistance=220 package=THT]
  LED2 = LED - 5mm [color="Red (633nm)" package="5 mm [THT]"]
  LED3 = LED - 5mm [color="Yellow (595nm)" package="5 mm [THT]"]
  J1 = Piezo Speaker

nets:
  N1: Componente1.D8, S3.Pin_1, S3.Pin_2, R2.Pin_0
  N2: Componente1.D10_PWM/SS, S2.Pin_3, S2.Pin_4, R3.Pin_1
  N3: Componente1.D11_PWM/MOSI, LED2.anode
  N4: Componente1.D2, S1.Pin_1, S1.Pin_2, R1.Pin_0
  N5: Componente1.D3_PWM, LED1.anode
  N6: Componente1.D5_PWM, J1.pin2
  N7: Componente1.D7, LED3.anode
  N8: Componente1.5V, S1.Pin_3, S1.Pin_4, S2.Pin_1, S2.Pin_2, S3.Pin_3, S3.Pin_4
  N9: Componente1.GND, R1.Pin_1, LED1.cathode, R2.Pin_1, R3.Pin_0, LED2.cathode, LED3.cathode, J1.pin1

// code stored in the sketch: pass_or_repass.ino
#define ledA 3
#define buttonA 2

#define ledB 11
#define buttonB 12

#define buttonReset 8

#define bzz 5

#define ledReset 7

int buttonA_read = 0;
int buttonB_read = 0;
int buttonReset_read = 0;

void setup() {
  pinMode(ledA, OUTPUT);
  pinMode(ledB, OUTPUT);

  pinMode(buttonA, INPUT);
  pinMode(buttonB, INPUT);
  pinMode(buttonReset, INPUT);

  pinMode(bzz, OUTPUT);
  
  pinMode(ledReset, OUTPUT);
  
  digitalWrite(ledReset, LOW);
  
  digitalWrite(bzz, HIGH);
  delay(250);
  digitalWrite(bzz, LOW);
  delay(250);
  digitalWrite(bzz, HIGH);
  delay(250);
  digitalWrite(bzz, LOW);
  delay(250);
  digitalWrite(bzz, HIGH);
  delay(300);
  digitalWrite(bzz, LOW);

  Serial.begin(9600);
}

void loop() {

  buttonA_read = digitalRead(buttonA);
  buttonB_read = digitalRead(buttonB);
  
  
  if (buttonA_read == HIGH) {
    Serial.write('A');
    digitalWrite(ledA, HIGH);
    digitalWrite(ledReset, HIGH);
    digitalWrite(bzz, HIGH);
    delay(500);
    digitalWrite(bzz, LOW);
    while(true) {
      buttonReset_read = digitalRead(buttonReset);
      if(buttonReset_read == HIGH) {
        digitalWrite(bzz, HIGH);
        delay(75);
        digitalWrite(bzz, LOW);
        digitalWrite(ledA, LOW);
        digitalWrite(ledReset, LOW);
        break;
      }
    }
  } else if (buttonB_read == HIGH) {
    Serial.write('B');
    digitalWrite(ledB, HIGH);
    digitalWrite(ledReset, HIGH);
    digitalWrite(bzz, HIGH);
    delay(500);
    digitalWrite(bzz, LOW);
    while(true) {
      buttonReset_read = digitalRead(buttonReset);
      if(buttonReset_read == HIGH) {
        digitalWrite(bzz, HIGH);
        delay(75);
        digitalWrite(bzz, LOW);
        digitalWrite(ledB, LOW);
        digitalWrite(ledReset, LOW);
        break;
      }
    }   
  }
}
